// Logisim project 4bit MUX Circ.circ as structural Verilog
module main (
  input  in_1,
  input  in_2,
  input  in_3,
  output out_4
);

  wire nand_1_out, nand_2_out, not_1_out;

  not not_1 (not_1_out, in_2);
  nand nand_1 (nand_1_out, in_1, not_1_out);
  nand nand_2 (nand_2_out, in_2, in_3);
  nand nand_3 (out_4, nand_1_out, nand_2_out);
endmodule

module mux (
  input  in_1,
  input  in_2,
  input  in_3,
  input  in_4,
  input  in_5,
  input  in_6,
  output out_7
);

  wire main_1_out_4, main_2_out_4;

  main main_1 (.in_1(in_1), .in_2(in_6), .in_3(in_2), .out_4(main_1_out_4));
  main main_2 (.in_1(in_3), .in_2(in_6), .in_3(in_4), .out_4(main_2_out_4));
  main main_3 (.in_1(main_1_out_4), .in_2(in_5), .in_3(main_2_out_4), .out_4(out_7));
endmodule
