// Logisim project AndNandORNor.circ as structural Verilog: 5 circuits, main circuit main
module main (
  input  in_1,
  input  in_2,
  input  in_3,
  input  in_4,
  input  in_5,
  input  in_6,
  input  in_7,
  input  in_8,
  output out_9,
  output out_10,
  output out_11,
  output out_12
);

  \and  and_1 (.in_1(in_1), .in_2(in_2), .out_3(out_9));
  \nand  nand_1 (.in_1(in_3), .in_2(in_4), .out_3(out_10));
  \or  or_1 (.in_1(in_6), .in_2(in_5), .out_3(out_11));
  \nor  nor_1 (.in_1(in_7), .in_2(in_8), .out_3(out_12));

  // Notes on the sheet:
  //   And
  //   Nand
  //   Or
  //   Nor
endmodule

module \and  (
  input  in_1,
  input  in_2,
  output out_3
);

  wire transistor_1_out;

  Transistor #(.\type ("n")) transistor_1 (.in(1'b1), .out(transistor_1_out), .gate(in_1));
  Transistor #(.\type ("n")) transistor_2 (.in(transistor_1_out), .out(out_3), .gate(in_2));
  Transistor transistor_3 (.in(1'b0), .out(out_3), .gate(in_1));
  Transistor transistor_4 (.in(1'b0), .out(out_3), .gate(in_2));
endmodule

module \nand  (
  input  in_1,
  input  in_2,
  output out_3
);

  wire transistor_1_out;

  Transistor #(.\type ("n")) transistor_1 (.in(1'b0), .out(transistor_1_out), .gate(in_1));
  Transistor #(.\type ("n")) transistor_2 (.in(transistor_1_out), .out(out_3), .gate(in_2));
  Transistor transistor_3 (.in(1'b1), .out(out_3), .gate(in_1));
  Transistor transistor_4 (.in(1'b1), .out(out_3), .gate(in_2));
endmodule

module \or  (
  input  in_1,
  input  in_2,
  output out_3
);

  wire transistor_1_out;

  Transistor transistor_1 (.in(1'b0), .out(transistor_1_out), .gate(in_1));
  Transistor transistor_2 (.in(transistor_1_out), .out(out_3), .gate(in_2));
  Transistor #(.\type ("n")) transistor_3 (.in(1'b1), .out(out_3), .gate(in_1));
  Transistor #(.\type ("n")) transistor_4 (.in(1'b1), .out(out_3), .gate(in_2));
endmodule

module \nor  (
  input  in_1,
  input  in_2,
  output out_3
);

  wire transistor_1_out;

  Transistor transistor_1 (.in(1'b1), .out(transistor_1_out), .gate(in_1));
  Transistor transistor_2 (.in(transistor_1_out), .out(out_3), .gate(in_2));
  Transistor #(.\type ("n")) transistor_3 (.in(1'b0), .out(out_3), .gate(in_1));
  Transistor #(.\type ("n")) transistor_4 (.in(1'b0), .out(out_3), .gate(in_2));
endmodule
