// Logisim project 4 bit MUX diag.circ as structural Verilog: 1 circuit, main circuit main
module main (
  input  a,
  input  b,
  input  A_2,
  input  B_2,
  input  C,
  input  D,
  output X
);

  wire and_1_out, and_2_out, and_3_out, and_4_out, and_5_out, and_6_out, and_7_out, and_8_out, not_1_out,
       not_2_out, not_3_out, not_4_out, or_1_out, or_2_out;

  not not_1 (not_1_out, a);
  not not_2 (not_2_out, a);
  and and_1 (and_1_out, A_2, not_1_out);
  not not_3 (not_3_out, b);
  and and_2 (and_2_out, B_2, not_2_out);
  and and_3 (and_3_out, C, a);
  not not_4 (not_4_out, b);
  and and_4 (and_4_out, D, a);
  and and_5 (and_5_out, and_1_out, not_3_out);
  and and_6 (and_6_out, and_2_out, b);
  and and_7 (and_7_out, and_3_out, not_4_out);
  and and_8 (and_8_out, and_4_out, b);
  or or_1 (or_1_out, and_5_out, and_6_out);
  or or_2 (or_2_out, and_7_out, and_8_out);
  or or_3 (X, or_1_out, or_2_out);
endmodule
