// Logisim project D flipflop.circ as structural Verilog: 3 circuits, main circuit main
module main (
  input  in_1,
  input  in_2,
  output out_3
);

  wire nand_1_out, nand_2_out, nand_4_out;

  nand nand_1 (nand_1_out, in_1, in_2);
  nand nand_2 (nand_2_out, nand_1_out, in_2);
  nand nand_3 (out_3, nand_1_out, nand_4_out);
  nand nand_4 (nand_4_out, out_3, nand_2_out);
endmodule

module series (
  input  in_1,
  input  in_2,
  output out_3,
  output out_4,
  output out_5,
  output out_6
);

  main main_1 (.in_1(in_1), .out_3(out_3), .in_2(in_2));
  main main_2 (.in_1(out_3), .out_3(out_4), .in_2(in_2));
  main main_3 (.in_1(out_4), .out_3(out_5), .in_2(in_2));
  main main_4 (.in_1(out_5), .out_3(out_6), .in_2(in_2));
endmodule

module parallel (
  input  in_1,
  input  in_2,
  input  in_3,
  input  in_4,
  input  in_5,
  output out_6,
  output out_7,
  output out_8,
  output out_9
);

  main main_1 (.in_1(in_1), .out_3(out_6), .in_2(in_2));
  main main_2 (.in_1(in_3), .out_3(out_7), .in_2(in_2));
  main main_3 (.in_1(in_4), .out_3(out_8), .in_2(in_2));
  main main_4 (.in_1(in_5), .out_3(out_9), .in_2(in_2));
endmodule
