// Logisim project Decoder.circ as structural Verilog
module Decoder (
  input  [31:0] in_1,
  output [6:0] opcode,
  output [4:0] rd,
  output [2:0] f3,
  output [4:0] rs1,
  output [4:0] rs2,
  output [6:0] f7,
  output [20:0] out_8
);

  wire [2:0] type_1_out_2;
  wire [20:0] bit_extender_1_out, bit_extender_2_out, bit_extender_3_out, bit_extender_4_out;
  wire [24:0] demultiplexer_1_out1;
  wire [31:0] demultiplexer_1_out2, demultiplexer_1_out3, demultiplexer_1_out4, demultiplexer_1_out5,
       demultiplexer_1_out6;

  Demultiplexer #(.select(3), .width(32)) demultiplexer_1 (
    .out1({f7, demultiplexer_1_out1}), .out2(demultiplexer_1_out2), .out3(demultiplexer_1_out3),
    .out4(demultiplexer_1_out4), .out5(demultiplexer_1_out5), .out6(demultiplexer_1_out6), .in(in_1),
    .sel(type_1_out_2));  // open: out0, out7, en
  Type type_1 (.in_1(in_1), .out_2(type_1_out_2));
  assign bit_extender_1_out = {{9{1'b0}}, {demultiplexer_1_out3[31:25], demultiplexer_1_out3[11:7]}};  // Bit_Extender bit_extender_1
  assign bit_extender_2_out = {{9{1'b0}}, demultiplexer_1_out2[31:20]};  // Bit_Extender bit_extender_2
  assign bit_extender_3_out = {{8{1'b0}}, {demultiplexer_1_out4[31], demultiplexer_1_out4[29:25], demultiplexer_1_out4[11:7], demultiplexer_1_out4[30], 1'b0}};  // Bit_Extender bit_extender_3
  assign bit_extender_4_out = {{1{1'b0}}, demultiplexer_1_out5[31:12]};  // Bit_Extender bit_extender_4
  Multiplexer #(.select(3), .width(5)) multiplexer_1 (
    .in1(demultiplexer_1_out1[11:7]), .in2(demultiplexer_1_out2[11:7]), .in5(demultiplexer_1_out5[11:7]),
    .in6(demultiplexer_1_out6[11:7]), .out(rd), .sel(type_1_out_2));  // open: in0, in3, in4, in7, en
  Multiplexer #(.select(3), .width(3)) multiplexer_2 (
    .in1(demultiplexer_1_out1[14:12]), .in2(demultiplexer_1_out2[14:12]), .in3(demultiplexer_1_out3[14:12]),
    .in4(demultiplexer_1_out4[14:12]), .out(f3), .sel(type_1_out_2));  // open: in0, in5, in6, in7, en
  Multiplexer #(.select(3), .width(5)) multiplexer_3 (
    .in1(demultiplexer_1_out1[19:15]), .in2(demultiplexer_1_out2[19:15]), .in3(demultiplexer_1_out3[19:15]),
    .in4(demultiplexer_1_out4[19:15]), .out(rs1), .sel(type_1_out_2));  // open: in0, in5, in6, in7, en
  Multiplexer #(.select(3), .width(5)) multiplexer_4 (
    .in1(demultiplexer_1_out1[24:20]), .in3(demultiplexer_1_out3[24:20]), .in4(demultiplexer_1_out4[24:20]),
    .out(rs2), .sel(type_1_out_2));  // open: in0, in2, in5, in6, in7, en
  Multiplexer #(.select(3), .width(21)) multiplexer_5 (
    .in2(bit_extender_2_out), .in3(bit_extender_1_out), .in4(bit_extender_3_out), .in5(bit_extender_4_out),
    .in6({demultiplexer_1_out6[31], demultiplexer_1_out6[21:12], demultiplexer_1_out6[22], demultiplexer_1_out6[30:23], 1'b0}),
    .out(out_8), .sel(type_1_out_2));  // open: in0, in1, in7, en

  assign opcode = in_1[6:0];

  // Notes on the sheet:
  //   R
  //   I
  //   F7
  //   IMM 11:5
  //   OPCODE
  //   RD
  //   F3
  //   RS1
  //   RS2
  //   OPCODE
  //   RD
  //   F3
  //   RS1
  //   IMMI
  //   OPCODE
  //   IMM 4:0
  //   F3
  //   RS1
  //   RS2
  //   OPCODE
  //   IMM 4:1|11
  //   F3
  //   RS1
  //   RS2
  //   IMM 12| 10:5
  //   OPCODE
  //   RD
  //   IMM
  //   OPCODE
  //   RD
  //   IMM
endmodule

module Type (
  input  [31:0] in_1,
  output [2:0] out_2
);

  wire comparator_1_eq, comparator_2_eq, comparator_3_eq, comparator_4_eq, comparator_5_eq, comparator_6_eq,
       comparator_7_eq, comparator_8_eq, comparator_9_eq, comparator_10_eq, comparator_11_eq,
       comparator_12_eq, or_1_out, or_2_out;

  Comparator #(.width(7)) comparator_1 (.a(in_1[6:0]), .b(7'b0110011), .eq(comparator_1_eq));  // open: gt, lt
  Comparator #(.width(7)) comparator_2 (.a(in_1[6:0]), .b(7'b0111011), .eq(comparator_2_eq));  // open: gt, lt
  or or_1 (or_1_out, comparator_1_eq, comparator_2_eq);
  Comparator #(.width(7)) comparator_3 (.a(in_1[6:0]), .b(7'b0000011), .eq(comparator_3_eq));  // open: gt, lt
  Comparator #(.width(7)) comparator_4 (.a(in_1[6:0]), .b(7'b0001111), .eq(comparator_4_eq));  // open: gt, lt
  Comparator #(.width(7)) comparator_5 (.a(in_1[6:0]), .b(7'b0010011), .eq(comparator_5_eq));  // open: gt, lt
  Comparator #(.width(7)) comparator_6 (.a(in_1[6:0]), .b(7'b0011011), .eq(comparator_6_eq));  // open: gt, lt
  Comparator #(.width(7)) comparator_7 (.a(in_1[6:0]), .b(7'b1100111), .eq(comparator_7_eq));  // open: gt, lt
  Comparator #(.width(7)) comparator_8 (.a(in_1[6:0]), .b(7'b1110011), .eq(comparator_8_eq));  // open: gt, lt
  or or_2 (or_2_out, comparator_3_eq, comparator_4_eq, comparator_5_eq, comparator_6_eq, comparator_7_eq, comparator_8_eq);
  Comparator #(.width(7)) comparator_9 (.a(in_1[6:0]), .b(7'b0100011), .eq(comparator_9_eq));  // open: gt, lt
  Comparator #(.width(7)) comparator_10 (.a(in_1[6:0]), .b(7'b1100011), .eq(comparator_10_eq));  // open: gt, lt
  Comparator #(.width(7)) comparator_11 (.a(in_1[6:0]), .b(7'b0110111), .eq(comparator_11_eq));  // open: gt, lt
  Comparator #(.width(7)) comparator_12 (.a(in_1[6:0]), .b(7'b1101111), .eq(comparator_12_eq));  // open: gt, lt
  en en_1 ();
  encoder encoder_1 (
    .F(comparator_12_eq), .out_7(out_2), .E(comparator_11_eq), .D(comparator_10_eq), .C(comparator_9_eq),
    .B(or_2_out), .A(or_1_out));

  // Notes on the sheet:
  //   R
  //   I
  //   S
  //   SB
  //   U
  //   UJ
endmodule

module encoder (
  input  F,
  input  E,
  input  D,
  input  C,
  input  B,
  input  A,
  output [2:0] out_7
);

  or or_1 (out_7[2], D, E, F);
  or or_2 (out_7[1], B, C, F);
  or or_3 (out_7[0], A, C, E);
endmodule

module experiment (
  input  [31:0] in_1,
  input  [31:0] in_2,
  output [6:0] Opcode,
  output [4:0] RD,
  output [2:0] Func_3,
  output [4:0] RS1,
  output [4:0] RS2,
  output [6:0] Func_7,
  output [19:0] IMM,
  output [6:0] Opcode_2,
  output [4:0] RD_2,
  output [2:0] Func_3_2,
  output [4:0] rs1_2,
  output [4:0] rs2_2,
  output [6:0] Func_7_2
);

  wire [2:0] type_1_out_2;
  wire [31:0] demultiplexer_1_out1, demultiplexer_1_out2, demultiplexer_1_out3, demultiplexer_1_out4,
       demultiplexer_1_out5, demultiplexer_1_out6;

  Demultiplexer #(.select(3), .width(32)) demultiplexer_1 (
    .out1(demultiplexer_1_out1), .out2(demultiplexer_1_out2), .out3(demultiplexer_1_out3),
    .out4(demultiplexer_1_out4), .out5(demultiplexer_1_out5), .out6(demultiplexer_1_out6), .in(in_2),
    .sel(type_1_out_2));  // open: out0, out7, en
  Type type_1 (.in_1(in_2), .out_2(type_1_out_2));
  // Decoder decoder_1: pin names not known; wires that end beside it: in_1, Opcode, RD, Func_3, RS1, RS2, Func_7, IMM
  Multiplexer #(.select(3), .width(32)) multiplexer_1 (
    .in1(demultiplexer_1_out1), .in2(demultiplexer_1_out2), .in3(demultiplexer_1_out3),
    .in4({demultiplexer_1_out4[31], demultiplexer_1_out4[29:25], demultiplexer_1_out4[11], demultiplexer_1_out4[24:12], demultiplexer_1_out4[10:7], demultiplexer_1_out4[30], demultiplexer_1_out4[6:0]}),
    .in5(demultiplexer_1_out5),
    .in6({demultiplexer_1_out6[31], demultiplexer_1_out6[21:12], demultiplexer_1_out6[22], demultiplexer_1_out6[30:23], demultiplexer_1_out6[11:0]}),
    .out({Func_7_2, rs2_2, rs1_2, Func_3_2, RD_2, Opcode_2}), .sel(type_1_out_2));  // open: in0, in7, en

  // Notes on the sheet:
  //   R
  //   I
  //   IMM 12| 10:5
  //   OPCODE
  //   IMM 4:1|11
  //   F3
  //   RS1
  //   RS2
  //   OPCODE
  //   RD
  //   IMM
endmodule
