// Logisim project Register File.circ as structural Verilog: 2 circuits, main circuit main
module main (
  input  Enable,
  input  [31:0] INPUT,
  input  [4:0] in_3,
  input  [4:0] in_4,
  input  [4:0] in_5,
  output [31:0] out_6,
  output [31:0] out_7
);

  wire demultiplexer_1_out1, demultiplexer_1_out2, demultiplexer_1_out3, demultiplexer_1_out4,
       demultiplexer_1_out5, demultiplexer_1_out6, demultiplexer_1_out7, demultiplexer_1_out8,
       demultiplexer_1_out9, demultiplexer_1_out10, demultiplexer_1_out11, demultiplexer_1_out12,
       demultiplexer_1_out13, demultiplexer_1_out14, demultiplexer_1_out15, demultiplexer_1_out16,
       demultiplexer_1_out17, demultiplexer_1_out18, demultiplexer_1_out19, demultiplexer_1_out20,
       demultiplexer_1_out21, demultiplexer_1_out22, demultiplexer_1_out23, demultiplexer_1_out24,
       demultiplexer_1_out25, demultiplexer_1_out26, demultiplexer_1_out27, demultiplexer_1_out28,
       demultiplexer_1_out29, demultiplexer_1_out30, demultiplexer_1_out31;
  wire [31:0] register_1_q, register_2_q, register_3_q, register_4_q, register_5_q, register_6_q,
       register_7_q, register_8_q, register_9_q, register_10_q, register_11_q, register_12_q, register_13_q,
       register_14_q, register_15_q, register_16_q, register_17_q, register_18_q, register_19_q,
       register_20_q, register_21_q, register_22_q, register_23_q, register_24_q, register_25_q,
       register_26_q, register_27_q, register_28_q, register_29_q, register_30_q, register_31_q,
       register_32_q;

  Demultiplexer #(.select(5)) demultiplexer_1 (
    .out1(demultiplexer_1_out1), .out2(demultiplexer_1_out2), .out3(demultiplexer_1_out3),
    .out4(demultiplexer_1_out4), .out5(demultiplexer_1_out5), .out6(demultiplexer_1_out6),
    .out7(demultiplexer_1_out7), .out8(demultiplexer_1_out8), .out9(demultiplexer_1_out9),
    .out10(demultiplexer_1_out10), .out11(demultiplexer_1_out11), .out12(demultiplexer_1_out12),
    .out13(demultiplexer_1_out13), .out14(demultiplexer_1_out14), .out15(demultiplexer_1_out15),
    .out16(demultiplexer_1_out16), .out17(demultiplexer_1_out17), .out18(demultiplexer_1_out18),
    .out19(demultiplexer_1_out19), .out20(demultiplexer_1_out20), .out21(demultiplexer_1_out21),
    .out22(demultiplexer_1_out22), .out23(demultiplexer_1_out23), .out24(demultiplexer_1_out24),
    .out25(demultiplexer_1_out25), .out26(demultiplexer_1_out26), .out27(demultiplexer_1_out27),
    .out28(demultiplexer_1_out28), .out29(demultiplexer_1_out29), .out30(demultiplexer_1_out30),
    .out31(demultiplexer_1_out31), .in(Enable), .sel(in_3));  // open: out0, en
  Register #(.width(32)) register_1 (.D(INPUT), .Q(register_1_q), .clk(1'b0));  // open: en, clr
  Register #(.width(32)) register_2 (.D(INPUT), .Q(register_2_q), .clk(demultiplexer_1_out4));  // open: en, clr
  Register #(.width(32)) register_3 (.D(INPUT), .Q(register_3_q), .clk(demultiplexer_1_out8));  // open: en, clr
  Register #(.width(32)) register_4 (.D(INPUT), .Q(register_4_q), .clk(demultiplexer_1_out12));  // open: en, clr
  Register #(.width(32)) register_5 (.D(INPUT), .Q(register_5_q), .clk(demultiplexer_1_out16));  // open: en, clr
  Register #(.width(32)) register_6 (.D(INPUT), .Q(register_6_q), .clk(demultiplexer_1_out20));  // open: en, clr
  Register #(.width(32)) register_7 (.D(INPUT), .Q(register_7_q), .clk(demultiplexer_1_out24));  // open: en, clr
  Register #(.width(32)) register_8 (.D(INPUT), .Q(register_8_q), .clk(demultiplexer_1_out28));  // open: en, clr
  Register #(.width(32)) register_9 (.D(INPUT), .Q(register_9_q), .clk(demultiplexer_1_out1));  // open: en, clr
  Register #(.width(32), .trigger("falling")) register_10 (
    .D(INPUT), .Q(register_10_q), .clk(demultiplexer_1_out5));  // open: en, clr
  Register #(.width(32)) register_11 (.D(INPUT), .Q(register_11_q), .clk(demultiplexer_1_out9));  // open: en, clr
  Register #(.width(32)) register_12 (.D(INPUT), .Q(register_12_q), .clk(demultiplexer_1_out13));  // open: en, clr
  Register #(.width(32)) register_13 (.D(INPUT), .Q(register_13_q), .clk(demultiplexer_1_out17));  // open: en, clr
  Register #(.width(32)) register_14 (.D(INPUT), .Q(register_14_q), .clk(demultiplexer_1_out21));  // open: en, clr
  Register #(.width(32)) register_15 (.D(INPUT), .Q(register_15_q), .clk(demultiplexer_1_out25));  // open: en, clr
  Register #(.width(32)) register_16 (.D(INPUT), .Q(register_16_q), .clk(demultiplexer_1_out29));  // open: en, clr
  Register #(.width(32)) register_17 (.D(INPUT), .Q(register_17_q), .clk(demultiplexer_1_out2));  // open: en, clr
  Register #(.width(32)) register_18 (.D(INPUT), .Q(register_18_q), .clk(demultiplexer_1_out6));  // open: en, clr
  Register #(.width(32)) register_19 (.D(INPUT), .Q(register_19_q), .clk(demultiplexer_1_out10));  // open: en, clr
  Register #(.width(32)) register_20 (.D(INPUT), .Q(register_20_q), .clk(demultiplexer_1_out14));  // open: en, clr
  Register #(.width(32)) register_21 (.D(INPUT), .Q(register_21_q), .clk(demultiplexer_1_out18));  // open: en, clr
  Register #(.width(32)) register_22 (.D(INPUT), .Q(register_22_q), .clk(demultiplexer_1_out22));  // open: en, clr
  Register #(.width(32)) register_23 (.D(INPUT), .Q(register_23_q), .clk(demultiplexer_1_out26));  // open: en, clr
  Register #(.width(32)) register_24 (.D(INPUT), .Q(register_24_q), .clk(demultiplexer_1_out30));  // open: en, clr
  Register #(.width(32)) register_25 (.D(INPUT), .Q(register_25_q), .clk(demultiplexer_1_out3));  // open: en, clr
  Register #(.width(32)) register_26 (.D(INPUT), .Q(register_26_q), .clk(demultiplexer_1_out7));  // open: en, clr
  Register #(.width(32)) register_27 (.D(INPUT), .Q(register_27_q), .clk(demultiplexer_1_out11));  // open: en, clr
  Register #(.width(32)) register_28 (.D(INPUT), .Q(register_28_q), .clk(demultiplexer_1_out15));  // open: en, clr
  Register #(.width(32)) register_29 (.D(INPUT), .Q(register_29_q), .clk(demultiplexer_1_out19));  // open: en, clr
  Register #(.width(32)) register_30 (.D(INPUT), .Q(register_30_q), .clk(demultiplexer_1_out23));  // open: en, clr
  Register #(.width(32)) register_31 (.D(INPUT), .Q(register_31_q), .clk(demultiplexer_1_out27));  // open: en, clr
  Register #(.width(32)) register_32 (.D(INPUT), .Q(register_32_q), .clk(demultiplexer_1_out31));  // open: en, clr
  Multiplexer #(.select(5), .width(32)) multiplexer_1 (
    .in0(register_1_q), .in1(register_9_q), .in2(register_17_q), .in3(register_25_q), .in4(register_2_q),
    .in5(register_10_q), .in6(register_18_q), .in7(register_26_q), .in8(register_3_q), .in9(register_11_q),
    .in10(register_19_q), .in11(register_27_q), .in12(register_4_q), .in13(register_12_q),
    .in14(register_20_q), .in15(register_28_q), .in16(register_5_q), .in17(register_13_q),
    .in18(register_21_q), .in19(register_29_q), .in20(register_6_q), .in21(register_14_q),
    .in22(register_22_q), .in23(register_30_q), .in24(register_7_q), .in25(register_15_q),
    .in26(register_23_q), .in27(register_31_q), .in28(register_8_q), .in29(register_16_q),
    .in30(register_24_q), .in31(register_32_q), .out(out_6), .sel(in_4));  // open: en
  Multiplexer #(.select(5), .width(32)) multiplexer_2 (
    .in0(register_1_q), .in1(register_9_q), .in2(register_17_q), .in3(register_25_q), .in4(register_2_q),
    .in5(register_10_q), .in6(register_18_q), .in7(register_26_q), .in8(register_3_q), .in9(register_11_q),
    .in10(register_19_q), .in11(register_27_q), .in12(register_4_q), .in13(register_12_q),
    .in14(register_20_q), .in15(register_28_q), .in16(register_5_q), .in17(register_13_q),
    .in18(register_21_q), .in19(register_29_q), .in20(register_6_q), .in21(register_14_q),
    .in22(register_22_q), .in23(register_30_q), .in24(register_7_q), .in25(register_15_q),
    .in26(register_23_q), .in27(register_31_q), .in28(register_8_q), .in29(register_16_q),
    .in30(register_24_q), .in31(register_32_q), .out(out_7), .sel(in_5));  // open: en
endmodule

module d (
  input  [31:0] in_1,
  input  in_2,
  input  [4:0] in_3,
  output [31:0] out_4,
  output [31:0] out_5
);

  wire undriven_2, undriven_3, undriven_4, undriven_5, undriven_6, undriven_7, undriven_8, undriven_9,
       undriven_16, undriven_17, undriven_18, undriven_19, undriven_20, undriven_21, undriven_22,
       undriven_23, undriven_30, undriven_31, undriven_32, undriven_33, undriven_34, undriven_35,
       undriven_36, undriven_37, undriven_46, undriven_47, undriven_48, undriven_49, undriven_50,
       undriven_51, undriven_52, undriven_53;
  wire [4:0] undriven;
  wire [31:0] demultiplexer_1_out1, demultiplexer_1_out2, demultiplexer_1_out3, demultiplexer_1_out4,
       demultiplexer_1_out5, demultiplexer_1_out6, demultiplexer_1_out7, demultiplexer_1_out8,
       demultiplexer_1_out9, demultiplexer_1_out10, demultiplexer_1_out11, demultiplexer_1_out12,
       demultiplexer_1_out13, demultiplexer_1_out14, demultiplexer_1_out15, demultiplexer_1_out16,
       demultiplexer_1_out17, demultiplexer_1_out18, demultiplexer_1_out19, demultiplexer_1_out20,
       demultiplexer_1_out21, demultiplexer_1_out22, demultiplexer_1_out23, demultiplexer_1_out24,
       demultiplexer_1_out25, demultiplexer_1_out26, demultiplexer_1_out27, demultiplexer_1_out28,
       demultiplexer_1_out29, demultiplexer_1_out30, demultiplexer_1_out31, register_1_q, register_2_q,
       register_3_q, register_4_q, register_5_q, register_6_q, register_7_q, register_8_q, register_9_q,
       register_10_q, register_11_q, register_12_q, register_13_q, register_14_q, register_15_q,
       register_16_q, register_17_q, register_18_q, register_19_q, register_20_q, register_21_q,
       register_22_q, register_23_q, register_24_q, register_25_q, register_26_q, register_27_q,
       register_28_q, register_29_q, register_30_q, register_31_q, register_32_q, undriven_10, undriven_11,
       undriven_12, undriven_13, undriven_14, undriven_15, undriven_24, undriven_25, undriven_26,
       undriven_27, undriven_28, undriven_29, undriven_38, undriven_39, undriven_40, undriven_41,
       undriven_42, undriven_43, undriven_44, undriven_45;

  Demultiplexer #(.select(5), .width(32)) demultiplexer_1 (
    .out1(demultiplexer_1_out1), .out2(demultiplexer_1_out2), .out3(demultiplexer_1_out3),
    .out4(demultiplexer_1_out4), .out5(demultiplexer_1_out5), .out6(demultiplexer_1_out6),
    .out7(demultiplexer_1_out7), .out8(demultiplexer_1_out8), .out9(demultiplexer_1_out9),
    .out10(demultiplexer_1_out10), .out11(demultiplexer_1_out11), .out12(demultiplexer_1_out12),
    .out13(demultiplexer_1_out13), .out14(demultiplexer_1_out14), .out15(demultiplexer_1_out15),
    .out16(demultiplexer_1_out16), .out17(demultiplexer_1_out17), .out18(demultiplexer_1_out18),
    .out19(demultiplexer_1_out19), .out20(demultiplexer_1_out20), .out21(demultiplexer_1_out21),
    .out22(demultiplexer_1_out22), .out23(demultiplexer_1_out23), .out24(demultiplexer_1_out24),
    .out25(demultiplexer_1_out25), .out26(demultiplexer_1_out26), .out27(demultiplexer_1_out27),
    .out28(demultiplexer_1_out28), .out29(demultiplexer_1_out29), .out30(demultiplexer_1_out30),
    .out31(demultiplexer_1_out31), .in(in_1), .sel(undriven));  // open: out0, en
  Register #(.width(32)) register_1 (.D({32{1'b0}}), .Q(register_1_q), .clk(undriven_2));  // open: en, clr
  Register #(.width(32)) register_2 (.D(demultiplexer_1_out4), .Q(register_2_q), .clk(undriven_3));  // open: en, clr
  Register #(.width(32)) register_3 (.D(demultiplexer_1_out8), .Q(register_3_q), .clk(undriven_4));  // open: en, clr
  Register #(.width(32)) register_4 (.D(demultiplexer_1_out12), .Q(register_4_q), .clk(undriven_5));  // open: en, clr
  Register #(.width(32)) register_5 (.D(demultiplexer_1_out16), .Q(register_5_q), .clk(undriven_6));  // open: en, clr
  Register #(.width(32)) register_6 (.D(demultiplexer_1_out20), .Q(register_6_q), .clk(undriven_7));  // open: en, clr
  Register #(.width(32)) register_7 (.D(demultiplexer_1_out24), .Q(register_7_q), .clk(undriven_8));  // open: en, clr
  Register #(.width(32)) register_8 (.D(demultiplexer_1_out28), .Q(register_8_q), .clk(undriven_9));  // open: en, clr
  Register #(.width(32), .trigger("falling")) register_9 (
    .D(demultiplexer_1_out1), .Q(register_9_q), .clk(undriven_16));  // open: en, clr
  Register #(.width(32)) register_10 (.D(demultiplexer_1_out5), .Q(register_10_q), .clk(undriven_17));  // open: en, clr
  Register #(.width(32)) register_11 (.D(undriven_10), .Q(register_11_q), .clk(undriven_18));  // open: en, clr
  Register #(.width(32)) register_12 (.D(undriven_11), .Q(register_12_q), .clk(undriven_19));  // open: en, clr
  Register #(.width(32)) register_13 (.D(undriven_12), .Q(register_13_q), .clk(undriven_20));  // open: en, clr
  Register #(.width(32)) register_14 (.D(undriven_13), .Q(register_14_q), .clk(undriven_21));  // open: en, clr
  Register #(.width(32)) register_15 (.D(undriven_14), .Q(register_15_q), .clk(undriven_22));  // open: en, clr
  Register #(.width(32)) register_16 (.D(undriven_15), .Q(register_16_q), .clk(undriven_23));  // open: en, clr
  Register #(.width(32)) register_17 (.D(demultiplexer_1_out2), .Q(register_17_q), .clk(undriven_30));  // open: en, clr
  Register #(.width(32)) register_18 (.D(demultiplexer_1_out6), .Q(register_18_q), .clk(undriven_31));  // open: en, clr
  Register #(.width(32)) register_19 (.D(undriven_24), .Q(register_19_q), .clk(undriven_32));  // open: en, clr
  Register #(.width(32)) register_20 (.D(undriven_25), .Q(register_20_q), .clk(undriven_33));  // open: en, clr
  Register #(.width(32)) register_21 (.D(undriven_26), .Q(register_21_q), .clk(undriven_34));  // open: en, clr
  Register #(.width(32)) register_22 (.D(undriven_27), .Q(register_22_q), .clk(undriven_35));  // open: en, clr
  Register #(.width(32)) register_23 (.D(undriven_28), .Q(register_23_q), .clk(undriven_36));  // open: en, clr
  Register #(.width(32)) register_24 (.D(undriven_29), .Q(register_24_q), .clk(undriven_37));  // open: en, clr
  Register #(.width(32)) register_25 (.D(undriven_38), .Q(register_25_q), .clk(undriven_46));  // open: en, clr
  Register #(.width(32)) register_26 (.D(undriven_39), .Q(register_26_q), .clk(undriven_47));  // open: en, clr
  Register #(.width(32)) register_27 (.D(undriven_40), .Q(register_27_q), .clk(undriven_48));  // open: en, clr
  Register #(.width(32)) register_28 (.D(undriven_41), .Q(register_28_q), .clk(undriven_49));  // open: en, clr
  Register #(.width(32)) register_29 (.D(undriven_42), .Q(register_29_q), .clk(undriven_50));  // open: en, clr
  Register #(.width(32)) register_30 (.D(undriven_43), .Q(register_30_q), .clk(undriven_51));  // open: en, clr
  Register #(.width(32)) register_31 (.D(undriven_44), .Q(register_31_q), .clk(undriven_52));  // open: en, clr
  Register #(.width(32)) register_32 (.D(undriven_45), .Q(register_32_q), .clk(undriven_53));  // open: en, clr
  Multiplexer #(.select(5), .width(32)) multiplexer_1 (
    .in4(register_1_q), .in5(register_9_q), .in6(register_17_q), .in7(register_25_q), .in8(register_2_q),
    .in9(register_10_q), .in10(register_18_q), .in11(register_26_q), .in12(register_3_q),
    .in13(register_11_q), .in14(register_19_q), .in15(register_27_q), .in16(register_4_q),
    .in17(register_12_q), .in18(register_20_q), .in19(register_28_q), .in20(register_5_q),
    .in21(register_13_q), .in22(register_21_q), .in23(register_29_q), .in24(register_6_q),
    .in25(register_14_q), .in26(register_22_q), .in27(register_30_q), .in28(register_7_q),
    .in29(register_15_q), .in30(register_23_q), .in31(register_31_q));  // open: in0, in1, in2, in3, out, sel, en
  Multiplexer #(.select(5), .width(32)) multiplexer_2 (
    .in4(register_1_q), .in5(register_9_q), .in6(register_17_q), .in7(register_25_q), .in8(register_2_q),
    .in9(register_10_q), .in10(register_18_q), .in11(register_26_q), .in12(register_3_q),
    .in13(register_11_q), .in14(register_19_q), .in15(register_27_q), .in16(register_4_q),
    .in17(register_12_q), .in18(register_20_q), .in19(register_28_q), .in20(register_5_q),
    .in21(register_13_q), .in22(register_21_q), .in23(register_29_q), .in24(register_6_q),
    .in25(register_14_q), .in26(register_22_q), .in27(register_30_q), .in28(register_7_q),
    .in29(register_15_q), .in30(register_23_q), .in31(register_31_q));  // open: in0, in1, in2, in3, out, sel, en
endmodule
