// Logisim project lw and sw.circ as structural Verilog: 2 circuits, main circuit lw and sw
module lw_and_sw (
  input  in_1,
  input  in_2,
  input  [31:0] in_3,
  input  in_4,
  input  in_5,
  input  in_6
);

  wire [2:0] decoder_1_f3;
  wire [4:0] decoder_1_rd, decoder_1_rs1, decoder_1_rs2;
  wire [6:0] decoder_1_f7;
  wire [20:0] decoder_1_out_8;
  wire [31:0] bit_extender_1_out, main_1_out_7, multiplexer_1_out, n32_bit_alu_1_p1, n32_bit_alu_1_p4,
       ram_1_data;

  Decoder decoder_1 (
    .in_1(in_3), .rd(decoder_1_rd), .f3(decoder_1_f3), .rs1(decoder_1_rs1), .rs2(decoder_1_rs2),
    .f7(decoder_1_f7), .out_8(decoder_1_out_8));  // open: opcode
  assign bit_extender_1_out = {{11{1'b0}}, decoder_1_out_8};  // Bit_Extender bit_extender_1
  Multiplexer #(.width(32)) multiplexer_1 (
    .in0(main_1_out_7), .in1(bit_extender_1_out), .out(multiplexer_1_out), .sel(in_1));  // open: en
  // _32_bit_ALU 32_bit_alu_1: pin names not known; wires that end beside it: n32_bit_alu_1_p1, multiplexer_1_out, {decoder_1_f7[0], decoder_1_f3}, n32_bit_alu_1_p4
  Register_File_main main_1 (
    .Enable(in_6), .INPUT(ram_1_data), .in_3(decoder_1_rd), .in_4(decoder_1_rs1), .in_5(decoder_1_rs2),
    .out_6(n32_bit_alu_1_p1), .out_7(main_1_out_7));
  RAM #(.addrWidth(24), .dataWidth(32), .bus("separate")) ram_1 (
    .addr(n32_bit_alu_1_p4[23:0]), .din(main_1_out_7), .data(ram_1_data), .str(in_2), .sel(in_4), .ld(in_5));  // open: clk, clr
endmodule

module control_unit (
  input  in_1,
  input  [6:0] opcode,
  input  [4:0] rs2
);

  wire and_1_out, comparator_1_eq;

  Comparator #(.width(7)) comparator_1 (.a(opcode), .b(7'b0100011), .eq(comparator_1_eq));  // open: gt, lt
  and and_1 (and_1_out, comparator_1_eq, in_1);
endmodule
