// Logisim project Processor.circ as structural Verilog: 10 circuits, main circuit Single Cycle Processor
module Single_Cycle_Processor (
  input  in_1,
  input  in_2,
  input  in_3
);

  wire control_decode_1_auipc_en, control_decode_1_jal_en, control_decode_1_jalr_en, control_decode_1_lui,
       control_decode_1_memread, control_decode_1_memwrite, control_decode_1_operandb_sel,
       control_decode_1_regwrite, or_1_out, or_2_out;
  wire [2:0] decoder_1_f3;
  wire [4:0] decoder_1_rd, decoder_1_rs1, decoder_1_rs2, multiplexer_3_out;
  wire [4:4] control_decode_1_branch;
  wire [6:0] decoder_1_f7, decoder_1_opcode;
  wire [23:0] alu_1_out_4;
  wire [31:0] adder_1_out, adder_2_out, adder_3_out, decoder_1_out_8, multiplexer_1_out, multiplexer_2_out,
       multiplexer_4_out, multiplexer_5_out, multiplexer_6_out, multiplexer_7_out, multiplexer_8_out,
       ram_1_data, register_1_q, register_file_1_out_7, register_file_1_out_8, rom_1_data, shifter_1_out,
       shifter_2_out;
  wire [31:24] alu_1_out_4_2;

  Shifter #(.width(32)) shifter_1 (.in(decoder_1_out_8), .\dist (5'b01100), .out(shifter_1_out));
  Multiplexer #(.width(32)) multiplexer_1 (
    .in0(adder_3_out), .in1({alu_1_out_4_2, alu_1_out_4}), .out(multiplexer_1_out),
    .sel(control_decode_1_jalr_en));  // open: en
  Shifter #(.width(32)) shifter_2 (.in(decoder_1_out_8), .\dist (5'b00001), .out(shifter_2_out));
  Adder #(.width(32)) adder_1 (.a(shifter_1_out), .b(register_1_q), .out(adder_1_out));  // open: cin, cout
  Adder #(.width(32)) adder_2 (.a(shifter_2_out), .b(register_1_q), .out(adder_2_out));  // open: cin, cout
  Multiplexer #(.width(32)) multiplexer_2 (
    .in0(multiplexer_1_out), .in1(adder_2_out), .out(multiplexer_2_out), .sel(control_decode_1_jal_en));  // open: en
  Register #(.width(32)) register_1 (.D(multiplexer_2_out), .Q(register_1_q), .clk(in_1), .clr(in_2));  // open: en
  Adder #(.width(32)) adder_3 (.a(register_1_q), .b(32'h4), .out(adder_3_out));  // open: cin, cout
  ROM #(.addrWidth(24), .dataWidth(32)) rom_1 (.addr(register_1_q[25:2]), .data(rom_1_data));  // open: sel
  Decoder decoder_1 (
    .in_1(rom_1_data), .opcode(decoder_1_opcode), .rd(decoder_1_rd), .f3(decoder_1_f3), .rs1(decoder_1_rs1),
    .rs2(decoder_1_rs2), .f7(decoder_1_f7), .out_8(decoder_1_out_8));
  Multiplexer #(.width(5)) multiplexer_3 (
    .in0(decoder_1_rd), .in1(5'b00001), .out(multiplexer_3_out), .sel(control_decode_1_jal_en));  // open: en
  Control_Decode control_decode_1 (
    .in_1(decoder_1_opcode), .Memwrite(control_decode_1_memwrite), .Branch(control_decode_1_branch[4]),
    .Memread(control_decode_1_memread), .Regwrite(control_decode_1_regwrite),
    .Mem_to_Reg(control_decode_1_memread), .OperandB_sel(control_decode_1_operandb_sel),
    .Jal_En(control_decode_1_jal_en), .Jalr_En(control_decode_1_jalr_en),
    .auipc_En(control_decode_1_auipc_en), .LUI(control_decode_1_lui));  // open: ALU_OP, Extend_Select, Next_Pc_Select
  or or_1 (or_1_out, control_decode_1_jal_en, control_decode_1_jalr_en);
  Multiplexer #(.width(32)) multiplexer_4 (
    .in0({alu_1_out_4_2, alu_1_out_4}), .in1(adder_3_out), .out(multiplexer_4_out), .sel(or_1_out));  // open: en
  // Probe on multiplexer_7_out
  // Probe on multiplexer_3_out
  // Probe on decoder_1_rs1
  // Probe on decoder_1_rs2
  Multiplexer #(.width(32)) multiplexer_5 (
    .in0(multiplexer_4_out), .in1(adder_1_out), .out(multiplexer_5_out), .sel(control_decode_1_auipc_en));  // open: en
  Multiplexer #(.width(32)) multiplexer_6 (
    .in0(multiplexer_5_out), .in1(shifter_1_out), .out(multiplexer_6_out), .sel(control_decode_1_lui));  // open: en
  Multiplexer #(.width(32)) multiplexer_7 (
    .in0(multiplexer_6_out), .in1(ram_1_data), .out(multiplexer_7_out), .sel(control_decode_1_memread));  // open: en
  Register_File register_file_1 (
    .Enable(control_decode_1_regwrite), .INPUT(multiplexer_7_out), .in_3(multiplexer_3_out),
    .in_4(decoder_1_rs1), .in_6(decoder_1_rs2), .out_7(register_file_1_out_7), .out_8(register_file_1_out_8),
    .in_5(in_2));
  // Probe on register_file_1_out_7
  // Probe on register_file_1_out_8
  Multiplexer #(.width(32)) multiplexer_8 (
    .in0(register_file_1_out_8), .in1(decoder_1_out_8), .out(multiplexer_8_out),
    .sel(control_decode_1_operandb_sel));  // open: en
  // Probe on {alu_1_out_4_2, alu_1_out_4}
  ALU alu_1 (
    .in_1(register_file_1_out_7), .in_2(multiplexer_8_out), .out_4({alu_1_out_4_2, alu_1_out_4}),
    .in_3({control_decode_1_branch[4], decoder_1_f7[5], decoder_1_f3}));
  or or_2 (or_2_out, control_decode_1_memwrite, control_decode_1_memread);
  RAM #(.addrWidth(24), .dataWidth(32), .bus("separate")) ram_1 (
    .addr(alu_1_out_4), .din(register_file_1_out_8), .data(ram_1_data), .str(control_decode_1_memwrite),
    .sel(or_2_out), .clk(in_1), .ld(control_decode_1_memread), .clr(in_2));

  // Notes on the sheet:
  //   contents of rom_1 (hex, n*v repeats v):
  //   d00e93 c00293 a00313 6283b3 ff5ff0ef
  //   Memory Unit
endmodule

module ALU (
  input  [31:0] in_1,
  input  [31:0] in_2,
  input  [4:0] in_3,
  output [31:0] out_4
);

  wire comparator_1_eq, comparator_1_gt, comparator_1_lt, comparator_2_gt, comparator_2_lt, comparator_3_lt,
       comparator_4_lt, not_1_out;
  wire [31:0] adder_1_out, and_1_out, bit_extender_1_out, bit_extender_2_out, bit_extender_3_out,
       bit_extender_4_out, bit_extender_5_out, bit_extender_6_out, bit_extender_7_out, bit_extender_8_out,
       or_1_out, shifter_1_out, shifter_2_out, shifter_3_out, subtractor_1_out, xor_1_out;

  assign or_1_out = in_1 | in_2;  // OR_Gate or_1, 32 bits wide
  assign and_1_out = in_1 & in_2;  // AND_Gate and_1, 32 bits wide
  assign xor_1_out = in_1 ^ in_2;  // XOR_Gate xor_1, 32 bits wide
  Adder #(.width(32)) adder_1 (.a(in_1), .b(in_2), .out(adder_1_out));  // open: cin, cout
  Subtractor #(.width(32)) subtractor_1 (.a(in_1), .b(in_2), .out(subtractor_1_out));  // open: bin, bout
  Comparator #(.width(32)) comparator_1 (
    .a(in_1), .b(in_2), .gt(comparator_1_gt), .eq(comparator_1_eq), .lt(comparator_1_lt));
  Comparator #(.width(32), .mode("unsigned")) comparator_2 (
    .a(in_1), .b(in_2), .gt(comparator_2_gt), .lt(comparator_2_lt));  // open: eq
  Comparator #(.width(32)) comparator_3 (.a(in_1), .b(in_2), .lt(comparator_3_lt));  // open: gt, eq
  Comparator #(.width(32), .mode("unsigned")) comparator_4 (.a(in_1), .b(in_2), .lt(comparator_4_lt));  // open: gt, eq
  Shifter #(.width(32)) shifter_1 (.in(in_1), .\dist (in_2[4:0]), .out(shifter_1_out));
  Shifter #(.width(32), .shift("lr")) shifter_2 (.in(in_1), .\dist (in_2[4:0]), .out(shifter_2_out));
  Shifter #(.width(32), .shift("ar")) shifter_3 (.in(in_1), .\dist (in_2[4:0]), .out(shifter_3_out));
  assign bit_extender_1_out = {{31{1'b0}}, comparator_1_eq};  // Bit_Extender bit_extender_1
  not not_1 (not_1_out, comparator_1_eq);
  assign bit_extender_2_out = {{31{1'b0}}, comparator_1_lt};  // Bit_Extender bit_extender_2
  assign bit_extender_3_out = {{31{1'b0}}, comparator_2_lt};  // Bit_Extender bit_extender_3
  assign bit_extender_4_out = {{31{1'b0}}, not_1_out};  // Bit_Extender bit_extender_4
  assign bit_extender_5_out = {{31{1'b0}}, comparator_1_gt};  // Bit_Extender bit_extender_5
  assign bit_extender_6_out = {{31{1'b0}}, comparator_2_gt};  // Bit_Extender bit_extender_6
  assign bit_extender_7_out = {{31{1'b0}}, comparator_3_lt};  // Bit_Extender bit_extender_7
  assign bit_extender_8_out = {{31{1'b0}}, comparator_4_lt};  // Bit_Extender bit_extender_8
  Multiplexer #(.select(5), .width(32)) multiplexer_1 (
    .in0(adder_1_out), .in1(shifter_1_out), .in2(bit_extender_7_out), .in3(bit_extender_8_out),
    .in4(xor_1_out), .in5(shifter_2_out), .in6(or_1_out), .in7(and_1_out), .in8(subtractor_1_out),
    .in12(shifter_3_out), .in16(bit_extender_1_out), .in17(bit_extender_4_out), .in18(bit_extender_2_out),
    .in19(bit_extender_5_out), .in20(bit_extender_3_out), .in21(bit_extender_6_out), .out(out_4), .sel(in_3));  // open: in9, in10, in11, in13, in14, in15, in22, in23, in24, in25, in26, in27, in28, in29, in30, in31, en

  // Notes on the sheet:
  //   OR
  //   And
  //   XOR
  //   ADD
  //   SUB
  //   BLT/SLT
  //   SLTU
  //   SLL
  //   SRL
  //   SRA
endmodule

module Fetch_Unit (
  input  in_1,
  input  in_2,
  output [31:0] out_3
);

  wire [31:0] adder_1_out, register_1_q;

  Register #(.width(32)) register_1 (.D(adder_1_out), .Q(register_1_q), .clk(in_2), .clr(in_1));  // open: en
  Adder #(.width(32)) adder_1 (.a(register_1_q), .b(32'h4), .out(adder_1_out));  // open: cin, cout
  ROM #(.addrWidth(24), .dataWidth(32)) rom_1 (.addr(register_1_q[25:2]), .data(out_3));  // open: sel
endmodule

module Encoder (
  input  F,
  input  E,
  input  D,
  input  C,
  input  B,
  input  A,
  output [2:0] out_7
);

  or or_1 (out_7[2], D, E, F);
  or or_2 (out_7[1], B, C, F);
  or or_3 (out_7[0], A, C, E);
endmodule

module Type_Identifier (
  input  [31:0] in_1,
  output [2:0] out_2,
  output out_3,
  output out_4,
  output out_5
);

  wire comparator_1_eq, comparator_2_eq, comparator_4_eq, comparator_5_eq, comparator_6_eq, comparator_7_eq,
       comparator_9_eq, comparator_10_eq, comparator_12_eq, comparator_13_eq, or_1_out, or_2_out;

  Comparator #(.width(7)) comparator_1 (.a(in_1[6:0]), .b(7'b0110011), .eq(comparator_1_eq));  // open: gt, lt
  Comparator #(.width(7)) comparator_2 (.a(in_1[6:0]), .b(7'b0111011), .eq(comparator_2_eq));  // open: gt, lt
  or or_1 (or_1_out, comparator_1_eq, comparator_2_eq);
  Comparator #(.width(7)) comparator_3 (.a(in_1[6:0]), .b(7'b0000011), .eq(out_3));  // open: gt, lt
  Comparator #(.width(7)) comparator_4 (.a(in_1[6:0]), .b(7'b0001111), .eq(comparator_4_eq));  // open: gt, lt
  Comparator #(.width(7)) comparator_5 (.a(in_1[6:0]), .b(7'b0010011), .eq(comparator_5_eq));  // open: gt, lt
  Comparator #(.width(7)) comparator_6 (.a(in_1[6:0]), .b(7'b0011011), .eq(comparator_6_eq));  // open: gt, lt
  Comparator #(.width(7)) comparator_7 (.a(in_1[6:0]), .b(7'b1110011), .eq(comparator_7_eq));  // open: gt, lt
  Comparator #(.width(7)) comparator_8 (.a(in_1[6:0]), .b(7'b1100111), .eq(out_5));  // open: gt, lt
  or or_2 (or_2_out, out_3, comparator_4_eq, comparator_5_eq, comparator_6_eq, comparator_7_eq);
  Comparator #(.width(7)) comparator_9 (.a(in_1[6:0]), .b(7'b0100011), .eq(comparator_9_eq));  // open: gt, lt
  Comparator #(.width(7)) comparator_10 (.a(in_1[6:0]), .b(7'b1100011), .eq(comparator_10_eq));  // open: gt, lt
  Comparator #(.width(7)) comparator_11 (.a(in_1[6:0]), .b(7'b0010111), .eq(out_4));  // open: gt, lt
  Comparator #(.width(7)) comparator_12 (.a(in_1[6:0]), .b(7'b0110111), .eq(comparator_12_eq));  // open: gt, lt
  Comparator #(.width(7)) comparator_13 (.a(in_1[6:0]), .b(7'b1101111), .eq(comparator_13_eq));  // open: gt, lt
  Encoder encoder_1 (
    .F(comparator_13_eq), .E(comparator_12_eq), .D(comparator_10_eq), .C(comparator_9_eq), .B(or_2_out),
    .A(or_1_out), .out_7(out_2));

  // Notes on the sheet:
  //   R
  //   I
  //   S
  //   SB
  //   U
  //   U
  //   UJ
endmodule

module Decoder (
  input  [31:0] in_1,
  output [6:0] opcode,
  output [4:0] rd,
  output [2:0] f3,
  output [4:0] rs1,
  output [4:0] rs2,
  output [6:0] f7,
  output [31:0] out_8
);

  wire [2:0] type_identifier_1_out_2;
  wire [20:0] bit_extender_1_out, bit_extender_2_out, bit_extender_3_out, bit_extender_4_out,
       multiplexer_5_out;
  wire [24:0] demultiplexer_1_out1;
  wire [31:0] demultiplexer_1_out2, demultiplexer_1_out3, demultiplexer_1_out4, demultiplexer_1_out5,
       demultiplexer_1_out6;

  Demultiplexer #(.select(3), .width(32)) demultiplexer_1 (
    .out1({f7, demultiplexer_1_out1}), .out2(demultiplexer_1_out2), .out3(demultiplexer_1_out3),
    .out4(demultiplexer_1_out4), .out5(demultiplexer_1_out5), .out6(demultiplexer_1_out6), .in(in_1),
    .sel(type_identifier_1_out_2));  // open: out0, out7, en
  Type_Identifier type_identifier_1 (.in_1(in_1), .out_2(type_identifier_1_out_2));  // open: out_3, out_4, out_5
  assign bit_extender_1_out = {{9{1'b0}}, {demultiplexer_1_out3[31:25], demultiplexer_1_out3[11:7]}};  // Bit_Extender bit_extender_1
  assign bit_extender_2_out = {{9{1'b0}}, demultiplexer_1_out2[31:20]};  // Bit_Extender bit_extender_2
  assign bit_extender_3_out = {{8{1'b0}}, {demultiplexer_1_out4[31], demultiplexer_1_out4[29:25], demultiplexer_1_out4[11:7], demultiplexer_1_out4[30], 1'b0}};  // Bit_Extender bit_extender_3
  assign bit_extender_4_out = {{1{1'b0}}, demultiplexer_1_out5[31:12]};  // Bit_Extender bit_extender_4
  Multiplexer #(.select(3), .width(5)) multiplexer_1 (
    .in1(demultiplexer_1_out1[11:7]), .in2(demultiplexer_1_out2[11:7]), .in5(demultiplexer_1_out5[11:7]),
    .in6(demultiplexer_1_out6[11:7]), .out(rd), .sel(type_identifier_1_out_2));  // open: in0, in3, in4, in7, en
  Multiplexer #(.select(3), .width(3)) multiplexer_2 (
    .in1(demultiplexer_1_out1[14:12]), .in2(demultiplexer_1_out2[14:12]), .in3(demultiplexer_1_out3[14:12]),
    .in4(demultiplexer_1_out4[14:12]), .out(f3), .sel(type_identifier_1_out_2));  // open: in0, in5, in6, in7, en
  Multiplexer #(.select(3), .width(5)) multiplexer_3 (
    .in1(demultiplexer_1_out1[19:15]), .in2(demultiplexer_1_out2[19:15]), .in3(demultiplexer_1_out3[19:15]),
    .in4(demultiplexer_1_out4[19:15]), .out(rs1), .sel(type_identifier_1_out_2));  // open: in0, in5, in6, in7, en
  Multiplexer #(.select(3), .width(5)) multiplexer_4 (
    .in1(demultiplexer_1_out1[24:20]), .in3(demultiplexer_1_out3[24:20]), .in4(demultiplexer_1_out4[24:20]),
    .out(rs2), .sel(type_identifier_1_out_2));  // open: in0, in2, in5, in6, in7, en
  assign out_8 = {{11{1'b0}}, multiplexer_5_out};  // Bit_Extender bit_extender_5
  Multiplexer #(.select(3), .width(21)) multiplexer_5 (
    .in2(bit_extender_2_out), .in3(bit_extender_1_out), .in4(bit_extender_3_out), .in5(bit_extender_4_out),
    .in6({demultiplexer_1_out6[31], demultiplexer_1_out6[21:12], demultiplexer_1_out6[22], demultiplexer_1_out6[30:23], 1'b0}),
    .out(multiplexer_5_out), .sel(type_identifier_1_out_2));  // open: in0, in1, in7, en

  assign opcode = in_1[6:0];

  // Notes on the sheet:
  //   R
  //   I
  //   OPCODE
  //   RD
  //   F3
  //   RS1
  //   RS2
  //   F7
  //   OPCODE
  //   RD
  //   F3
  //   RS1
  //   IMMI
  //   OPCODE
  //   IMM 4:0
  //   F3
  //   RS1
  //   RS2
  //   IMM 11:5
  //   IMM 4:1|11
  //   F3
  //   RS1
  //   RS2
  //   IMM 12| 10:5
  //   RD
  //   IMM
  //   RD
  //   IMM
endmodule

module Register_File (
  input  Enable,
  input  [31:0] INPUT,
  input  [4:0] in_3,
  input  [4:0] in_4,
  input  in_5,
  input  [4:0] in_6,
  output [31:0] out_7,
  output [31:0] out_8
);

  wire demultiplexer_1_out1, demultiplexer_1_out2, demultiplexer_1_out3, demultiplexer_1_out4,
       demultiplexer_1_out5, demultiplexer_1_out6, demultiplexer_1_out7, demultiplexer_1_out8,
       demultiplexer_1_out9, demultiplexer_1_out10, demultiplexer_1_out11, demultiplexer_1_out12,
       demultiplexer_1_out13, demultiplexer_1_out14, demultiplexer_1_out15, demultiplexer_1_out16,
       demultiplexer_1_out17, demultiplexer_1_out18, demultiplexer_1_out19, demultiplexer_1_out20,
       demultiplexer_1_out21, demultiplexer_1_out22, demultiplexer_1_out23, demultiplexer_1_out24,
       demultiplexer_1_out25, demultiplexer_1_out26, demultiplexer_1_out27, demultiplexer_1_out28,
       demultiplexer_1_out29, demultiplexer_1_out30, demultiplexer_1_out31;
  wire [31:0] register_1_q, register_2_q, register_3_q, register_4_q, register_5_q, register_6_q,
       register_7_q, register_8_q, register_9_q, register_10_q, register_11_q, register_12_q, register_13_q,
       register_14_q, register_15_q, register_16_q, register_17_q, register_18_q, register_19_q,
       register_20_q, register_21_q, register_22_q, register_23_q, register_24_q, register_25_q,
       register_26_q, register_27_q, register_28_q, register_29_q, register_30_q, register_31_q,
       register_32_q;

  Demultiplexer #(.select(5)) demultiplexer_1 (
    .out1(demultiplexer_1_out1), .out2(demultiplexer_1_out2), .out3(demultiplexer_1_out3),
    .out4(demultiplexer_1_out4), .out5(demultiplexer_1_out5), .out6(demultiplexer_1_out6),
    .out7(demultiplexer_1_out7), .out8(demultiplexer_1_out8), .out9(demultiplexer_1_out9),
    .out10(demultiplexer_1_out10), .out11(demultiplexer_1_out11), .out12(demultiplexer_1_out12),
    .out13(demultiplexer_1_out13), .out14(demultiplexer_1_out14), .out15(demultiplexer_1_out15),
    .out16(demultiplexer_1_out16), .out17(demultiplexer_1_out17), .out18(demultiplexer_1_out18),
    .out19(demultiplexer_1_out19), .out20(demultiplexer_1_out20), .out21(demultiplexer_1_out21),
    .out22(demultiplexer_1_out22), .out23(demultiplexer_1_out23), .out24(demultiplexer_1_out24),
    .out25(demultiplexer_1_out25), .out26(demultiplexer_1_out26), .out27(demultiplexer_1_out27),
    .out28(demultiplexer_1_out28), .out29(demultiplexer_1_out29), .out30(demultiplexer_1_out30),
    .out31(demultiplexer_1_out31), .in(Enable), .sel(in_3));  // open: out0, en
  Register #(.width(32)) register_1 (.D(INPUT), .Q(register_1_q), .clk(1'b0), .clr(in_5));  // open: en
  Register #(.width(32)) register_2 (.D(INPUT), .Q(register_2_q), .clk(demultiplexer_1_out4), .clr(in_5));  // open: en
  Register #(.width(32)) register_3 (.D(INPUT), .Q(register_3_q), .clk(demultiplexer_1_out8), .clr(in_5));  // open: en
  Register #(.width(32)) register_4 (.D(INPUT), .Q(register_4_q), .clk(demultiplexer_1_out12), .clr(in_5));  // open: en
  Register #(.width(32)) register_5 (.D(INPUT), .Q(register_5_q), .clk(demultiplexer_1_out16), .clr(in_5));  // open: en
  Register #(.width(32)) register_6 (.D(INPUT), .Q(register_6_q), .clk(demultiplexer_1_out20), .clr(in_5));  // open: en
  Register #(.width(32)) register_7 (.D(INPUT), .Q(register_7_q), .clk(demultiplexer_1_out24), .clr(in_5));  // open: en
  Register #(.width(32)) register_8 (.D(INPUT), .Q(register_8_q), .clk(demultiplexer_1_out28), .clr(in_5));  // open: en
  Register #(.width(32)) register_9 (.D(INPUT), .Q(register_9_q), .clk(demultiplexer_1_out1), .clr(in_5));  // open: en
  Register #(.width(32)) register_10 (
    .D(INPUT), .Q(register_10_q), .clk(demultiplexer_1_out5), .clr(in_5));  // open: en
  Register #(.width(32)) register_11 (
    .D(INPUT), .Q(register_11_q), .clk(demultiplexer_1_out9), .clr(in_5));  // open: en
  Register #(.width(32)) register_12 (
    .D(INPUT), .Q(register_12_q), .clk(demultiplexer_1_out13), .clr(in_5));  // open: en
  Register #(.width(32)) register_13 (
    .D(INPUT), .Q(register_13_q), .clk(demultiplexer_1_out17), .clr(in_5));  // open: en
  Register #(.width(32)) register_14 (
    .D(INPUT), .Q(register_14_q), .clk(demultiplexer_1_out21), .clr(in_5));  // open: en
  Register #(.width(32)) register_15 (
    .D(INPUT), .Q(register_15_q), .clk(demultiplexer_1_out25), .clr(in_5));  // open: en
  Register #(.width(32)) register_16 (
    .D(INPUT), .Q(register_16_q), .clk(demultiplexer_1_out29), .clr(in_5));  // open: en
  Register #(.width(32)) register_17 (
    .D(INPUT), .Q(register_17_q), .clk(demultiplexer_1_out2), .clr(in_5));  // open: en
  Register #(.width(32)) register_18 (
    .D(INPUT), .Q(register_18_q), .clk(demultiplexer_1_out6), .clr(in_5));  // open: en
  Register #(.width(32)) register_19 (
    .D(INPUT), .Q(register_19_q), .clk(demultiplexer_1_out10), .clr(in_5));  // open: en
  Register #(.width(32)) register_20 (
    .D(INPUT), .Q(register_20_q), .clk(demultiplexer_1_out14), .clr(in_5));  // open: en
  Register #(.width(32)) register_21 (
    .D(INPUT), .Q(register_21_q), .clk(demultiplexer_1_out18), .clr(in_5));  // open: en
  Register #(.width(32)) register_22 (
    .D(INPUT), .Q(register_22_q), .clk(demultiplexer_1_out22), .clr(in_5));  // open: en
  Register #(.width(32)) register_23 (
    .D(INPUT), .Q(register_23_q), .clk(demultiplexer_1_out26), .clr(in_5));  // open: en
  Register #(.width(32)) register_24 (
    .D(INPUT), .Q(register_24_q), .clk(demultiplexer_1_out30), .clr(in_5));  // open: en
  Register #(.width(32)) register_25 (
    .D(INPUT), .Q(register_25_q), .clk(demultiplexer_1_out3), .clr(in_5));  // open: en
  Register #(.width(32)) register_26 (
    .D(INPUT), .Q(register_26_q), .clk(demultiplexer_1_out7), .clr(in_5));  // open: en
  Register #(.width(32)) register_27 (
    .D(INPUT), .Q(register_27_q), .clk(demultiplexer_1_out11), .clr(in_5));  // open: en
  Register #(.width(32)) register_28 (
    .D(INPUT), .Q(register_28_q), .clk(demultiplexer_1_out15), .clr(in_5));  // open: en
  Register #(.width(32)) register_29 (
    .D(INPUT), .Q(register_29_q), .clk(demultiplexer_1_out19), .clr(in_5));  // open: en
  Register #(.width(32)) register_30 (
    .D(INPUT), .Q(register_30_q), .clk(demultiplexer_1_out23), .clr(in_5));  // open: en
  Register #(.width(32)) register_31 (
    .D(INPUT), .Q(register_31_q), .clk(demultiplexer_1_out27), .clr(in_5));  // open: en
  Register #(.width(32)) register_32 (
    .D(INPUT), .Q(register_32_q), .clk(demultiplexer_1_out31), .clr(in_5));  // open: en
  Multiplexer #(.select(5), .width(32)) multiplexer_1 (
    .in0(register_1_q), .in1(register_9_q), .in2(register_17_q), .in3(register_25_q), .in4(register_2_q),
    .in5(register_10_q), .in6(register_18_q), .in7(register_26_q), .in8(register_3_q), .in9(register_11_q),
    .in10(register_19_q), .in11(register_27_q), .in12(register_4_q), .in13(register_12_q),
    .in14(register_20_q), .in15(register_28_q), .in16(register_5_q), .in17(register_13_q),
    .in18(register_21_q), .in19(register_29_q), .in20(register_6_q), .in21(register_14_q),
    .in22(register_22_q), .in23(register_30_q), .in24(register_7_q), .in25(register_15_q),
    .in26(register_23_q), .in27(register_31_q), .in28(register_8_q), .in29(register_16_q),
    .in30(register_24_q), .in31(register_32_q), .out(out_7), .sel(in_4));  // open: en
  Multiplexer #(.select(5), .width(32)) multiplexer_2 (
    .in0(register_1_q), .in1(register_9_q), .in2(register_17_q), .in3(register_25_q), .in4(register_2_q),
    .in5(register_10_q), .in6(register_18_q), .in7(register_26_q), .in8(register_3_q), .in9(register_11_q),
    .in10(register_19_q), .in11(register_27_q), .in12(register_4_q), .in13(register_12_q),
    .in14(register_20_q), .in15(register_28_q), .in16(register_5_q), .in17(register_13_q),
    .in18(register_21_q), .in19(register_29_q), .in20(register_6_q), .in21(register_14_q),
    .in22(register_22_q), .in23(register_30_q), .in24(register_7_q), .in25(register_15_q),
    .in26(register_23_q), .in27(register_31_q), .in28(register_8_q), .in29(register_16_q),
    .in30(register_24_q), .in31(register_32_q), .out(out_8), .sel(in_6));  // open: en
endmodule

module Cu (
  input  [6:0] opcode,
  output R,
  output I,
  output S,
  output SB,
  output U,
  output UJ,
  output LOAD,
  output LUI,
  output Jalr
);

  wire [2:0] type_identifier_1_out_2;
  wire [31:0] bit_extender_1_out;

  assign bit_extender_1_out = {{25{1'b0}}, opcode};  // Bit_Extender bit_extender_1
  Demultiplexer #(.select(3)) demultiplexer_1 (
    .out1(R), .out2(I), .out3(S), .out4(SB), .out5(U), .out6(UJ), .in(1'b1), .sel(type_identifier_1_out_2));  // open: out0, out7, en
  Type_Identifier type_identifier_1 (
    .in_1(bit_extender_1_out), .out_2(type_identifier_1_out_2), .out_3(LOAD), .out_4(LUI), .out_5(Jalr));
endmodule

module Control_Decode (
  input  [6:0] in_1,
  output Memwrite,
  output Branch,
  output Memread,
  output Regwrite,
  output Mem_to_Reg,
  output [2:0] ALU_OP,
  output OperandB_sel,
  output Extend_Select,
  output Next_Pc_Select,
  output Jal_En,
  output Jalr_En,
  output auipc_En,
  output LUI
);

  wire cu_1_i, cu_1_r;

  Cu cu_1 (
    .opcode(in_1), .R(cu_1_r), .I(cu_1_i), .S(Extend_Select), .SB(Branch), .U(auipc_En), .UJ(Jal_En),
    .LOAD(Mem_to_Reg), .LUI(LUI), .Jalr(Jalr_En));
  or or_1 (Regwrite, Mem_to_Reg, cu_1_r, cu_1_i);
  or or_2 (OperandB_sel, cu_1_i, Extend_Select, Mem_to_Reg);
  Encoder encoder_1 (.F(1'b0), .E(Mem_to_Reg), .D(Branch), .C(Extend_Select), .B(cu_1_i), .A(cu_1_r), .out_7(ALU_OP));

  assign Memread = Mem_to_Reg;
  assign Memwrite = Extend_Select;
  assign Next_Pc_Select = Branch;
endmodule

module test_processor (
  input  in_1,
  input  in_2
);

  wire [2:0] decoder_1_f3;
  wire [4:0] decoder_1_rd, decoder_1_rs1, decoder_1_rs2;
  wire [6:0] decoder_1_f7, decoder_1_opcode;
  wire [31:0] adder_1_out, ram_1_data, register_1_q;

  Register #(.width(32)) register_1 (.D(adder_1_out), .Q(register_1_q), .clk(in_1), .clr(in_2));  // open: en
  Adder #(.width(32)) adder_1 (.a(register_1_q), .b(32'h4), .out(adder_1_out));  // open: cin, cout
  RAM #(.addrWidth(24), .dataWidth(32)) ram_1 (
    .addr(register_1_q[25:2]), .data(ram_1_data));  // open: sel, clk, ld, clr
  Decoder decoder_1 (
    .in_1(ram_1_data), .opcode(decoder_1_opcode), .rd(decoder_1_rd), .f3(decoder_1_f3), .rs1(decoder_1_rs1),
    .rs2(decoder_1_rs2), .f7(decoder_1_f7));  // open: out_8
  Control_Decode control_decode_1 (.in_1(decoder_1_opcode));  // open: Memwrite, Branch, Memread, Regwrite, Mem_to_Reg, ALU_OP, OperandB_sel, Extend_Select, Next_Pc_Select, Jal_En, Jalr_En, auipc_En, LUI
  Register_File register_file_1 (
    .in_3(decoder_1_rd), .in_4(decoder_1_rs1), .in_6(decoder_1_rs2));  // open: Enable, INPUT, out_7, out_8, in_5
endmodule
