// Logisim project latch.circ as structural Verilog: 1 circuit, main circuit main
module main (
  input  RESET,
  input  SET,
  output Q,
  output Q_prime
);

  nor nor_1 (Q, RESET, Q_prime);
  nor nor_2 (Q_prime, Q, SET);

  // Notes on the sheet:
  //   SR LATCH
endmodule
