// Logisim project comparator.circ as structural Verilog
module main (
  input  in_1,
  input  in_2,
  output A_B,
  output A_B_2,
  output A_B_3
);

  wire not_1_out, not_2_out;

  not not_1 (not_1_out, in_2);
  not not_2 (not_2_out, in_1);
  and and_1 (A_B, in_1, not_1_out);
  xnor xnor_1 (A_B_2, in_1, in_2);
  and and_2 (A_B_3, not_2_out, in_2);
endmodule

module _1_bit_comparator (
  input  A,
  input  B,
  output A_B,
  output A_B_2,
  output A_B_3
);

  main main_1 (.in_1(B), .in_2(A), .A_B(A_B_3), .A_B_2(A_B_2), .A_B_3(A_B));
endmodule
