// Logisim project full adder.circ as structural Verilog: 2 circuits, main circuit main
module main (
  input  in_1,
  input  in_2,
  input  in_3,
  output [1:0] out_4
);

  wire and_1_out, and_2_out, xor_1_out;

  xor xor_1 (xor_1_out, in_1, in_2);
  xor xor_2 (out_4[0], xor_1_out, in_3);
  and and_1 (and_1_out, in_3, xor_1_out);
  and and_2 (and_2_out, in_2, in_1);
  or or_1 (out_4[1], and_1_out, and_2_out);
endmodule

module IC (
  input  in_1,
  input  in_2,
  input  in_3,
  output [1:0] out_4
);

  // main main_1: pin names not known; wires that end beside it: in_1, in_2, in_3, out_4
endmodule
