// Logisim project half adder.circ as structural Verilog: 1 circuit, main circuit main
module main (
  input  in_1,
  input  in_2,
  input  [1:0] in_3
);

  and and_1 (in_3[1], in_1, in_2);
  xor xor_1 (in_3[0], in_1, in_2);

  // Notes on the sheet:
  //   CARRY
  //   SUM
endmodule
